# Fritzing sketch ItsyBitsyM4_audio (saved by Fritzing 0.9.6b)
breadboards: 1

parts:
  U1 = Adafruit ItsyBitsy M4 [part_number="Adafruit #3800"]
  J1 = TRRS 3.5mm Jack Breakout
  R1 = Resistor [tolerance=±5% resistance=1k package="2010 [SMD]"]
  C3 = Electrolytic Capacitor [capacitance=1µF voltage=35V package="100 mil [THT, electrolytic]"]

nets:
  GND: U1.GND, J1.SLEEVE, C3.-
  N1: U1.A0, R1.Pin_0
  N2: J1.RING1, J1.TIP, R1.Pin_1, C3.+

custom parts:
  Adafruit ItsyBitsy M4: What's smaller than a Feather but larger than a Trinket? It's an Adafruit ItsyBitsy M4 Express featuring the Microchip ATSAMD51! Small, powerful, with a ultra fast ATSAMD51 Cortex M4 processor running at 120 MHz - this microcontroller board is perfect when you want something very compact, with a ton of horsepower and a bunch of pins. This Itsy is like a bullet train, with it's 120MHz Cortex M4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
